// Logisim project cpu.circ as structural Verilog: 17 circuits, main circuit main
module main (
  input  IRQ0,
  input  IRQ1,
  input  IRQ2,
  input  IRQ3
);

  wire ALU_EN_D, ALU_IMM16, ALU_SEL_SRC, CARRY, Cin, CLK, CLK_low, EN_CAUSE, EN_ERET, EN_EXC_ADDR, EN_ISR,
       EN_STATUS, EN_X, IACK, ILL_RD, ILL_WR, ILLEGAL, INC_PC, INT_ENABLED, INT_PENDING, IO_BYTE, IO_LOAD,
       IO_STORE, LD_CAUSE, LD_ERET, LD_EXC_ADDR, LD_IMM16, LD_INST, LD_ISR, LD_PTB, LD_STATUS, LD_TIMER,
       MMU_DATA, MMU_SRC, MMU_ST, MODE, NEG, not_1_out, OVERF, PG_FLT, REG_LOAD, REG_X_SRC, RESET, SIGN_EXT,
       STATUS_SRC, TIME_OUT, TIMER_carry;
  wire [2:0] ALU_SEL, SEL_X;
  wire [3:0] ALU_STATUS;
  wire [7:0] CAUSE_out_7;
  wire [7:4] CAUSE;
  wire [8:0] control_1_out_7;
  wire [15:0] A_BUS, D_BUS, ERET_REG_out_7, EXC_ADDR_out_7, IMM16_dout, IMM16_out_7, INST, INST_out_7,
       ISR_out_7, multiplexer_1_out, multiplexer_4_out, PC, reg_unit_1_yout, reg_unit_1_zout, STATUS_out_7,
       TIMER_data, V_ADDR;
  wire [15:1] STATUS;
  wire [23:0] mmu_1_a_phys;

  LED led_1 (.in(MODE));
  LED led_2 (.in(CLK));
  Multiplexer #(.width(16), .enable("false")) multiplexer_1 (
    .in0(PC), .in1(A_BUS), .out(multiplexer_1_out), .sel(MMU_SRC));
  Multiplexer #(.width(3), .enable("false")) multiplexer_2 (
    .in0(INST[11:9]), .in1(3'b110), .out(ALU_SEL), .sel(ALU_SEL_SRC));
  Priority_Encoder #(.select(4)) priority_encoder_1 (
    .in0(1'b1), .in1(INT_PENDING), .in10(ILL_WR), .in11(ILL_RD), .in12(PG_FLT), .in13(ILLEGAL),
    .in14(TIME_OUT), .in15(not_1_out), .out(CAUSE));  // open: in2, in3, in4, in5, in6, in7, in8, in9, gs, en_out, en_in
  not not_1 (not_1_out, MODE);
  reg_8bit_tristate u_CAUSE (
    .in_1({CAUSE, IRQ3, IRQ2, IRQ1, IRQ0}), .LD(LD_CAUSE), .CLK(CLK), .RST(RESET), .out_7(CAUSE_out_7),
    .EN(EN_CAUSE), .out_6(D_BUS[7:0]));
  // Probe on CAUSE_out_7
  Multiplexer #(.width(3), .enable("false")) multiplexer_3 (
    .in0(INST[2:0]), .in1(3'b110), .out(SEL_X), .sel(REG_X_SRC));
  // Probe on CAUSE
  // Probe on D_BUS
  mmu mmu_1 (
    .Din(D_BUS), .Ain(multiplexer_1_out), .MODE(MODE), .MMU_ST(MMU_ST), .VMEM(STATUS[4]),
    .MMU_DATA(MMU_DATA), .IO_LOAD(IO_LOAD), .IO_STORE(IO_STORE), .LD_PTB(LD_PTB), .RESET(CLK), .CLK(RESET),
    .A_PHYS(mmu_1_a_phys), .PAGE_FAULT(PG_FLT), .ILLEGAL_WRITE(ILL_WR), .ILLEGAL_READ(ILL_RD));  // open: out_16
  // Probe on EXC_ADDR_out_7
  // Probe on D_BUS
  reg_tristate EXC_ADDR (
    .Din(V_ADDR), .LD(LD_EXC_ADDR), .CLK(CLK), .RST(RESET), .out_7(EXC_ADDR_out_7), .EN(EN_EXC_ADDR),
    .Dout(D_BUS));
  // Probe on mmu_1_a_phys
  // Probe on PC
  // Probe on A_BUS
  // Probe on ERET_REG_out_7
  mmio mmio_1 (
    .Din(D_BUS), .Addr(mmu_1_a_phys), .Dout(D_BUS), .Store(IO_STORE), .Load(IO_LOAD), .Byte(IO_BYTE),
    .SignExt(SIGN_EXT), .Clk(CLK));
  // Probe on control_1_out_7
  // Probe on INST
  reg_tristate ERET_REG (
    .Din(PC), .LD(LD_ERET), .CLK(CLK), .RST(RESET), .out_7(ERET_REG_out_7), .EN(EN_ERET), .Dout(D_BUS));
  // Probe on INST_out_7
  // Probe on D_BUS
  // Probe on A_BUS
  reg_tristate ISR (.Din(D_BUS), .LD(LD_ISR), .CLK(CLK), .RST(RESET), .out_7(ISR_out_7), .EN(EN_ISR), .Dout(D_BUS));
  // Probe on ISR_out_7
  reg_tristate u_INST (.Din(D_BUS), .LD(LD_INST), .CLK(CLK), .RST(RESET), .out_7(INST_out_7), .EN(1'b1), .Dout(INST));
  // Probe on PC
  control control_1 (
    .INST(INST), .STATUS({STATUS[15:6], INT_ENABLED, STATUS[4], OVERF, CARRY, STATUS[1], NEG}),
    .CAUSE_HI_4({CAUSE, IRQ3, IRQ2, IRQ1, IRQ0}), .ALU_Cin(Cin), .EN_ALU_D(ALU_EN_D),
    .ALU_SEL_SRC(ALU_SEL_SRC), .REG_LOAD(REG_LOAD), .EN_REG_X(EN_X), .REG_X_SRC(REG_X_SRC), .INC_PC(INC_PC),
    .ALU_IMM16(ALU_IMM16), .MMIO_STORE(IO_STORE), .MMIO_LOAD(IO_LOAD), .SIGN_EXT(SIGN_EXT),
    .MMIO_BYTE(IO_BYTE), .MMU_DATA(MMU_DATA), .MMU_ST(MMU_ST), .MMU_SRC(MMU_SRC), .LD_PTB(LD_PTB),
    .LD_IMM16(LD_IMM16), .LD_INST(LD_INST), .LD_CAUSE(LD_CAUSE), .EN_CAUSE(EN_CAUSE),
    .STATUS_SRC(STATUS_SRC), .EN_STATUS(EN_STATUS), .LD_STATUS(LD_STATUS), .LD_EXC_ADDR(LD_EXC_ADDR),
    .EN_EXC_ADDR(EN_EXC_ADDR), .LD_ERET(LD_ERET), .EN_ERET(EN_ERET), .IACK(IACK), .LD_TIMER(LD_TIMER),
    .LD_ISR(LD_ISR), .EN_ISR(EN_ISR), .RESET(RESET), .out_7(control_1_out_7), .CLK(CLK), .CLK_x(CLK_low),
    .INVALID_MODE(ILLEGAL), .MODE(MODE), .INT_PENDING(INT_PENDING));
  // Probe on IMM16_out_7
  Multiplexer #(.width(16), .enable("false")) multiplexer_4 (
    .in0({STATUS[15:6], INT_ENABLED, STATUS[4], ALU_STATUS}), .in1(D_BUS), .out(multiplexer_4_out),
    .sel(STATUS_SRC));
  reg_tristate IMM16 (
    .Din(D_BUS), .LD(LD_IMM16), .CLK(CLK), .RST(RESET), .out_7(IMM16_out_7), .EN(1'b1), .Dout(IMM16_dout));
  reg_tristate u_STATUS (
    .Din(multiplexer_4_out), .LD(LD_STATUS), .CLK(CLK), .RST(RESET), .out_7(STATUS_out_7), .EN(1'b1),
    .Dout({STATUS[15:6], INT_ENABLED, STATUS[4], OVERF, CARRY, STATUS[1], NEG}));
  // Probe on STATUS_out_7
  // Probe on SEL_X
  // Probe on INST[5:3]
  // Probe on INST[8:6]
  assign D_BUS = EN_STATUS ? {STATUS[15:6], INT_ENABLED, STATUS[4], OVERF, CARRY, STATUS[1], NEG} : 16'bz;  // Controlled_Buffer controlled_buffer_1
  reg_unit reg_unit_1 (
    .Din(D_BUS), .IMM16(IMM16_dout), .LOAD(REG_LOAD), .CLK_low(CLK_low), .SEL_X(SEL_X), .RST(RESET),
    .SEL_Y(INST[5:3]), .INC_PC(INC_PC), .SEL_Z(INST[8:6]), .EN_X(EN_X), .Xout(D_BUS), .Yout(reg_unit_1_yout),
    .Zout(reg_unit_1_zout), .PCout(PC));
  alu_16_bit alu_16_bit_1 (
    .Y(reg_unit_1_yout), .Z(reg_unit_1_zout), .Cin(Cin), .ALU_SEL(ALU_SEL), .EN_D(ALU_EN_D), .d_out(D_BUS),
    .a_out(A_BUS), .alu_status(ALU_STATUS));
  // Probe on ALU_SEL
  counter_16_bit TIMER (
    .Din(D_BUS), .LD_TIMER(LD_TIMER), .CLK(CLK), .RST(RESET), .DECR(MODE), .CARRY(TIMER_carry),
    .DATA(TIMER_data));
  // Probe on TIMER_data
  and and_1 (TIME_OUT, TIMER_carry, LD_INST);

  // Other names for the same wires on the sheet: CAUSE[3:0] = {IRQ3, IRQ2, IRQ1, IRQ0}; SEL_Y[2:0] = INST[5:3];
  //   SEL_Z[2:0] = INST[8:6]; STATUS (some bits) = {INT_ENABLED, OVERF, CARRY, NEG}; ZERO = STATUS[1];
  //   VMEM_ENABLED = STATUS[4]

  // Notes on the sheet:
  //   CPU
endmodule

module \reg  (
  input  [15:0] Din,
  input  EN_X_low,
  input  EN_Y_low,
  input  RST,
  input  EN_Z_low,
  input  LOAD_low,
  input  CLK_low,
  output [15:0] Xout,
  output [15:0] Yout,
  output [15:0] Zout,
  output [15:0] out_11
);

  wire nor_1_out, not_1_out, not_2_out, not_3_out;

  nor nor_1 (nor_1_out, EN_X_low, LOAD_low, CLK_low);
  Register #(.width(16)) register_1 (.D(Din), .clk(nor_1_out), .Q(out_11), .clr(RST));  // open: en
  not not_1 (not_1_out, EN_X_low);
  not not_2 (not_2_out, EN_Y_low);
  not not_3 (not_3_out, EN_Z_low);
  assign Xout = not_1_out ? out_11 : 16'bz;  // Controlled_Buffer controlled_buffer_1
  assign Yout = not_2_out ? out_11 : 16'bz;  // Controlled_Buffer controlled_buffer_2
  assign Zout = not_3_out ? out_11 : 16'bz;  // Controlled_Buffer controlled_buffer_3

  // Notes on the sheet:
  //   Single User Register
endmodule

// REG
module reg_unit (
  input  [15:0] Din,
  input  [2:0] SEL_X,
  input  [15:0] IMM16,
  input  EN_X,
  input  [2:0] SEL_Y,
  input  CLK_low,
  input  RST,
  input  INC_PC,
  input  LOAD,
  input  [2:0] SEL_Z,
  output [15:0] Xout,
  output [15:0] Yout,
  output [15:0] Zout,
  output [15:0] PCout
);

  wire decoder_1_out1, decoder_1_out2, decoder_1_out3, decoder_1_out4, decoder_1_out5, decoder_1_out6,
       decoder_1_out7, decoder_2_out1, decoder_2_out2, decoder_2_out3, decoder_2_out4, decoder_2_out5,
       decoder_2_out6, decoder_2_out7, decoder_3_out1, decoder_3_out2, decoder_3_out3, decoder_3_out4,
       decoder_3_out5, decoder_3_out6, decoder_3_out7, LOAD_t, not_2_out, not_3_out, not_4_out, not_5_out,
       not_6_out, not_7_out, not_8_out, not_9_out, not_10_out, not_11_out, not_12_out, not_13_out,
       not_14_out, not_15_out, not_16_out, not_17_out, not_18_out, not_19_out;
  wire [15:0] fp_out_11, pc_out_13, r1_out_11, r2_out_11, r3_out_11, sp_out_11, Xout_t;

  not not_1 (LOAD_t, LOAD);
  not not_2 (not_2_out, decoder_1_out1);
  not not_3 (not_3_out, decoder_1_out2);
  not not_4 (not_4_out, decoder_1_out3);
  not not_5 (not_5_out, decoder_1_out4);
  not not_6 (not_6_out, decoder_1_out5);
  not not_7 (not_7_out, decoder_1_out6);
  Decoder #(.select(3), .enable("false")) decoder_1 (
    .out1(decoder_1_out1), .out2(decoder_1_out2), .out3(decoder_1_out3), .out4(decoder_1_out4),
    .out5(decoder_1_out5), .out6(decoder_1_out6), .out7(decoder_1_out7), .sel(SEL_Y));  // open: out0
  \reg  r2 (
    .Din(Din), .EN_X_low(not_11_out), .EN_Y_low(not_3_out), .EN_Z_low(not_14_out), .LOAD_low(LOAD_t),
    .CLK_low(CLK_low), .RST(RST), .out_11(r2_out_11), .Xout(Xout_t), .Yout(Yout), .Zout(Zout));
  // Probe on r2_out_11
  \reg  fp (
    .Din(Din), .EN_X_low(not_12_out), .EN_Y_low(not_5_out), .EN_Z_low(not_17_out), .LOAD_low(LOAD_t),
    .CLK_low(CLK_low), .RST(RST), .out_11(fp_out_11), .Xout(Xout_t), .Yout(Yout), .Zout(Zout));
  // Probe on fp_out_11
  reg_pc pc (
    .RST(RST), .INC_PC(INC_PC), .CLK(CLK_low), .PCin(Din), .EN_X_low(not_18_out), .EN_Y_low(not_7_out),
    .EN_Z_low(not_19_out), .LOAD_low(LOAD_t), .out_13(pc_out_13), .Xout(Xout_t), .Yout(Yout), .Zout(Zout),
    .PCout(PCout));
  // Probe on pc_out_13
  Decoder #(.select(3)) decoder_2 (
    .out1(decoder_2_out1), .out2(decoder_2_out2), .out3(decoder_2_out3), .out4(decoder_2_out4),
    .out5(decoder_2_out5), .out6(decoder_2_out6), .out7(decoder_2_out7), .sel(SEL_X));  // open: out0, en
  not not_8 (not_8_out, decoder_2_out3);
  not not_9 (not_9_out, decoder_2_out5);
  not not_10 (not_10_out, decoder_2_out1);
  not not_11 (not_11_out, decoder_2_out2);
  not not_12 (not_12_out, decoder_2_out4);
  not not_13 (not_13_out, decoder_3_out1);
  not not_14 (not_14_out, decoder_3_out2);
  not not_15 (not_15_out, decoder_3_out3);
  not not_16 (not_16_out, decoder_3_out5);
  not not_17 (not_17_out, decoder_3_out4);
  Decoder #(.select(3), .enable("false")) decoder_3 (
    .out1(decoder_3_out1), .out2(decoder_3_out2), .out3(decoder_3_out3), .out4(decoder_3_out4),
    .out5(decoder_3_out5), .out6(decoder_3_out6), .out7(decoder_3_out7), .sel(SEL_Z));  // open: out0
  not not_18 (not_18_out, decoder_2_out6);
  not not_19 (not_19_out, decoder_3_out6);
  // Probe on r1_out_11
  // Probe on r3_out_11
  // Probe on sp_out_11
  \reg  r1 (
    .Din(Din), .EN_X_low(not_10_out), .EN_Y_low(not_2_out), .EN_Z_low(not_13_out), .LOAD_low(LOAD_t),
    .CLK_low(CLK_low), .RST(RST), .out_11(r1_out_11), .Xout(Xout_t), .Yout(Yout), .Zout(Zout));
  \reg  r3 (
    .Din(Din), .EN_X_low(not_8_out), .EN_Y_low(not_4_out), .EN_Z_low(not_15_out), .LOAD_low(LOAD_t),
    .CLK_low(CLK_low), .RST(RST), .out_11(r3_out_11), .Xout(Xout_t), .Yout(Yout), .Zout(Zout));
  \reg  sp (
    .Din(Din), .EN_X_low(not_9_out), .EN_Y_low(not_6_out), .EN_Z_low(not_16_out), .LOAD_low(LOAD_t),
    .CLK_low(CLK_low), .RST(RST), .out_11(sp_out_11), .Xout(Xout_t), .Yout(Yout), .Zout(Zout));
  assign Xout_t = decoder_2_out7 ? IMM16 : 16'bz;  // Controlled_Buffer controlled_buffer_1
  assign Yout = decoder_1_out7 ? IMM16 : 16'bz;  // Controlled_Buffer controlled_buffer_2
  assign Zout = decoder_3_out7 ? IMM16 : 16'bz;  // Controlled_Buffer controlled_buffer_3
  Pull_Resistor pull_resistor_1 (.node(Xout_t));
  assign Xout = EN_X ? Xout_t : 16'bz;  // Controlled_Buffer controlled_buffer_4
  Pull_Resistor pull_resistor_2 (.node(Yout));
  Pull_Resistor pull_resistor_3 (.node(Zout));

  // Notes on the sheet:
  //   Full Register Unit
endmodule

// CONTROL
module control (
  input  [15:0] INST,
  input  [15:0] STATUS,
  input  [7:0] CAUSE_HI_4,
  output CLK,
  output CLK_x,
  output INVALID_MODE,
  output [8:0] out_7,
  output MODE,
  output INT_PENDING,
  output ALU_Cin,
  output MMIO_STORE,
  output LD_CAUSE,
  output LD_EXC_ADDR,
  output EN_ALU_D,
  output MMIO_LOAD,
  output EN_CAUSE,
  output EN_EXC_ADDR,
  output ALU_SEL_SRC,
  output LD_ERET,
  output SIGN_EXT,
  output STATUS_SRC,
  output REG_LOAD,
  output EN_ERET,
  output MMIO_BYTE,
  output EN_STATUS,
  output EN_REG_X,
  output IACK,
  output MMU_DATA,
  output LD_STATUS,
  output REG_X_SRC,
  output LD_TIMER,
  output MMU_ST,
  output INC_PC,
  output LD_ISR,
  output MMU_SRC,
  output ALU_IMM16,
  output EN_ISR,
  output LD_PTB,
  output RESET,
  output LD_IMM16,
  output LD_INST
);

  wire and_1_out, and_2_out, and_3_out, and_4_out, and_5_out, and_6_out, and_7_out, COND_INV, COND_TRUE,
       decoder_1_out0, decoder_1_out1, decoder_1_out2, decoder_1_out3, decoder_1_out4, decoder_1_out5,
       decoder_1_out6, decoder_1_out7, FETCH, KERN_ONLY, not_2_out, NOT_INT_VEC, or_1_out, or_2_out,
       or_3_out, or_5_out, START, TOGGLE_MODE, TRAP_PENDING;
  wire [1:0] pull_resistor_1_node;
  wire [2:0] COND, rom_1_data_2;
  wire [6:4] rom_2_data;
  wire [8:0] bit_extender_1_out, multiplexer_1_out, NEXT;
  wire [28:14] rom_1_data;

  Decoder #(.select(3)) decoder_1 (
    .out0(decoder_1_out0), .out1(decoder_1_out1), .out2(decoder_1_out2), .out3(decoder_1_out3),
    .out4(decoder_1_out4), .out5(decoder_1_out5), .out6(decoder_1_out6), .out7(decoder_1_out7), .sel(COND));  // open: en
  not not_1 (START, STATUS[6]);
  assign bit_extender_1_out = {{5{1'b1}}, CAUSE_HI_4[7:4]};  // Bit_Extender bit_extender_1
  Pull_Resistor pull_resistor_1 (.node(pull_resistor_1_node));
  and and_1 (and_1_out, decoder_1_out1, STATUS[0]);
  and and_2 (and_2_out, decoder_1_out2, STATUS[1]);
  and and_3 (and_3_out, decoder_1_out3, STATUS[2]);
  and and_4 (and_4_out, decoder_1_out4, STATUS[3]);
  and and_5 (and_5_out, decoder_1_out5, or_1_out);
  or or_1 (or_1_out, STATUS[1], STATUS[0]);
  and and_6 (and_6_out, decoder_1_out6, TRAP_PENDING);
  and and_7 (and_7_out, decoder_1_out7, TRAP_PENDING, NOT_INT_VEC);
  Multiplexer #(.width(9), .disabled("Z")) multiplexer_1 (
    .in0(NEXT), .in1(bit_extender_1_out), .out(multiplexer_1_out), .sel(COND_TRUE), .en(not_2_out));
  Multiplexer #(.width(9), .disabled("Z")) multiplexer_2 (
    .in0({pull_resistor_1_node, INST[15:9]}), .in1(bit_extender_1_out), .out(multiplexer_1_out),
    .sel(COND_TRUE), .en(FETCH));
  or or_2 (or_2_out, CAUSE_HI_4[4], CAUSE_HI_4[5], CAUSE_HI_4[6], CAUSE_HI_4[7]);
  // Probe on multiplexer_1_out
  not not_2 (not_2_out, FETCH);
  or or_3 (or_3_out, decoder_1_out0, and_1_out, and_2_out, and_3_out, and_4_out, and_5_out, and_6_out, and_7_out);
  or or_4 (NOT_INT_VEC, ~CAUSE_HI_4[4], CAUSE_HI_4[5], CAUSE_HI_4[6], CAUSE_HI_4[7]);  // OR_Gate
  and and_8 (TRAP_PENDING, or_2_out, MODE);
  Register #(.width(9)) register_1 (.D(multiplexer_1_out), .clk(CLK_x), .Q(out_7));  // open: en, clr
  xor xor_1 (COND_TRUE, or_3_out, COND_INV);
  LED led_1 (.in(CLK));
  ROM #(.addrWidth(9), .dataWidth(32)) rom_1 (
    .addr(out_7),
    .data({COND[0], COND_INV, FETCH, rom_1_data[28:27], ALU_SEL_SRC, MMIO_BYTE, SIGN_EXT, rom_1_data_2, LD_STATUS, STATUS_SRC, rom_1_data[18], LD_ISR, LD_TIMER, IACK, rom_1_data[14], LD_EXC_ADDR, LD_IMM16, LD_INST, LD_PTB, MMU_SRC, MMU_ST, MMU_DATA, MMIO_LOAD, MMIO_STORE, INC_PC, ALU_IMM16, REG_X_SRC, REG_LOAD, ALU_Cin}));
  ROM #(.addrWidth(9), .dataWidth(16)) rom_2 (
    .addr(out_7), .data({NEXT, rom_2_data, KERN_ONLY, TOGGLE_MODE, COND[2:1]}));
  Clock clock_1 (.out(CLK));
  not not_3 (CLK_x, CLK);
  and and_9 (LD_ERET, rom_1_data[14], MODE);
  and and_10 (LD_CAUSE, rom_1_data[18], MODE);
  and and_11 (RESET, rom_2_data[4], CLK);
  Decoder #(.select(3), .enable("false")) decoder_2 (
    .out1(EN_EXC_ADDR), .out2(EN_ERET), .out3(EN_ISR), .out4(EN_STATUS), .out5(EN_CAUSE), .out6(EN_REG_X),
    .out7(EN_ALU_D), .sel(rom_1_data_2));  // open: out0
  J_K_Flip_Flop j_k_ff_1 (.J(TOGGLE_MODE), .K(TOGGLE_MODE), .clk(CLK), .Q(MODE));  // open: Qn, preset, reset
  or or_5 (or_5_out, CAUSE_HI_4[0], CAUSE_HI_4[1], CAUSE_HI_4[2], CAUSE_HI_4[3]);
  and and_12 (INVALID_MODE, KERN_ONLY, MODE);
  and and_13 (INT_PENDING, or_5_out, STATUS[5]);

  // Other names for the same wires on the sheet: Cin = ALU_Cin; CAUSE_LO_4[3:0] = CAUSE_HI_4[3:0];
  //   CAUSE_HI_4_t[3:0] = CAUSE_HI_4[7:4]; NEG = STATUS[0]; ZERO = STATUS[1]; CARRY = STATUS[2]; OVERF = STATUS[3];
  //   VMEM = STATUS[4]; INT_ENABLED = STATUS[5]

  // Notes on the sheet:
  //   Control Unit
  //   contents of rom_1 (hex, n*v repeats v):
  //   16*0 40000000 f00002 6*0 80041050 5*0 80045050 6*0 4044260 4044240 73*0 80040000 7*0 80040000 0
  //   80041050 0 80040000 80044000 131*0 4e10000 0 4f80000 800002 4c00220 4000242 4e00002 232*0 20047850
  //   14*0 60000850
  //   contents of rom_2 (hex, n*v repeats v):
  //   16*0 8381 7*0 803 5*0 8303 6*0 8283 8303 73*0 820b 7*0 800b 0 808b 0 818b 840b 130*0 4 239*0 3
  //   Internal Control Lines
  //   External Control Lines
  //   ALU
  //   <-- Reserves the bus for MMIO
  //   IO
  //   Some Exception Generators
  //   CAUSE
  //   STATUS
  //   EXCEPTIONS
endmodule

// ALU
module alu_4_bit (
  input  [3:0] Ain,
  input  [3:0] Bin,
  input  [2:0] S,
  input  Cin,
  output [3:0] Dout,
  output Cout
);

  wire [3:0] adder_1_out, and_1_out, or_1_out, subtractor_1_out, subtractor_2_out, xor_1_out;

  assign xor_1_out = Ain ^ Bin;  // XOR_Gate xor_1, 4 bits wide
  Subtractor #(.width(4)) subtractor_1 (.a(Bin), .b(Ain), .out(subtractor_1_out), .bin(Cin));  // open: bout
  assign and_1_out = Ain & Bin;  // AND_Gate and_1, 4 bits wide
  Subtractor #(.width(4)) subtractor_2 (.a(Ain), .b(Bin), .out(subtractor_2_out), .bin(Cin));  // open: bout
  assign or_1_out = Ain | Bin;  // OR_Gate or_1, 4 bits wide
  Adder #(.width(4)) adder_1 (.a(Ain), .b(Bin), .out(adder_1_out), .cin(Cin), .cout(Cout));
  Multiplexer #(.select(3), .width(4), .enable("false")) multiplexer_1 (
    .in0(4'b0000), .in1(xor_1_out), .in2(subtractor_1_out), .in3(and_1_out), .in4(subtractor_2_out),
    .in5(or_1_out), .in6(adder_1_out), .in7(4'b1111), .out(Dout), .sel(S));

  // Notes on the sheet:
  //   ALU (4 bit segment)
endmodule

// ALU
module alu_16_bit (
  input  [15:0] Y,
  input  [15:0] Z,
  input  Cin,
  input  [2:0] ALU_SEL,
  input  EN_D,
  output [15:0] d_out,
  output [15:0] a_out,
  output [3:0] alu_status
);

  wire _4_BIT_2_cout, _4_BIT_3_cout, _4_BIT_cout, and_1_out, and_2_out, EN_A, not_2_out, not_3_out, not_4_out;
  wire [2:0] _4_BIT_4_dout;
  wire [3:0] _4_BIT_2_dout, _4_BIT_3_dout, _4_BIT_dout;

  alu_4_bit _4_BIT (.Ain(Y[3:0]), .Bin(Z[3:0]), .Cin(Cin), .S(ALU_SEL), .Dout(_4_BIT_dout), .Cout(_4_BIT_cout));
  alu_4_bit _4_BIT_2 (
    .Ain(Y[7:4]), .Bin(Z[7:4]), .Cin(_4_BIT_cout), .S(ALU_SEL), .Dout(_4_BIT_2_dout), .Cout(_4_BIT_2_cout));
  alu_4_bit _4_BIT_3 (
    .Ain(Y[11:8]), .Bin(Z[11:8]), .Cin(_4_BIT_2_cout), .S(ALU_SEL), .Dout(_4_BIT_3_dout), .Cout(_4_BIT_3_cout));
  alu_4_bit _4_BIT_4 (
    .Ain(Y[15:12]), .Bin(Z[15:12]), .Cin(_4_BIT_3_cout), .S(ALU_SEL), .Dout({alu_status[0], _4_BIT_4_dout}),
    .Cout(alu_status[2]));
  not not_1 (EN_A, EN_D);
  not not_2 (not_2_out, alu_status[0]);
  and and_1 (and_1_out, not_2_out, Y[15], Z[15]);
  not not_3 (not_3_out, Y[15]);
  and and_2 (and_2_out, alu_status[0], not_3_out, not_4_out);
  not not_4 (not_4_out, Z[15]);
  assign d_out = EN_D ? {alu_status[0], _4_BIT_4_dout, _4_BIT_3_dout, _4_BIT_2_dout, _4_BIT_dout} : 16'bz;  // Controlled_Buffer controlled_buffer_1
  assign a_out = EN_A ? {alu_status[0], _4_BIT_4_dout, _4_BIT_3_dout, _4_BIT_2_dout, _4_BIT_dout} : 16'bz;  // Controlled_Buffer controlled_buffer_2
  nor nor_1 (alu_status[1], _4_BIT_dout[0], _4_BIT_dout[1], _4_BIT_dout[2], _4_BIT_dout[3], _4_BIT_2_dout[0], _4_BIT_2_dout[1], _4_BIT_2_dout[2], _4_BIT_2_dout[3], _4_BIT_3_dout[0], _4_BIT_3_dout[1], _4_BIT_3_dout[2], _4_BIT_3_dout[3], _4_BIT_4_dout[0], _4_BIT_4_dout[1], _4_BIT_4_dout[2], alu_status[0]);
  or or_1 (alu_status[3], and_1_out, and_2_out);

  // Notes on the sheet:
  //   ALU (Full 16 bit)
  //   zero
  //   neg
  //   carry
  //   over
endmodule

// MMU
module mmu (
  input  [15:0] Din,
  input  [15:0] Ain,
  input  MODE,
  input  IO_LOAD,
  input  IO_STORE,
  input  LD_PTB,
  input  RESET,
  input  CLK,
  input  MMU_ST,
  input  VMEM,
  input  MMU_DATA,
  output [23:0] A_PHYS,
  output PAGE_FAULT,
  output ILLEGAL_WRITE,
  output ILLEGAL_READ,
  output out_16
);

  wire and_1_out, and_2_out, nor_1_out, nor_2_out, not_1_out, not_2_out, not_3_out, or_1_out;
  wire [3:0] ram_1_data_2;
  wire [7:0] multiplexer_1_out, PTB_out_6, PTB_out_7;
  wire [11:0] ram_1_data;

  // Probe on PTB_out_7
  reg_8bit_tristate PTB (
    .in_1(Din[7:0]), .LD(LD_PTB), .CLK(CLK), .RST(RESET), .out_7(PTB_out_7), .EN(1'b1), .out_6(PTB_out_6));
  or or_1 (or_1_out, MODE, MMU_ST);
  Multiplexer #(.width(8), .enable("false")) multiplexer_1 (
    .in0({8{1'b0}}), .in1(PTB_out_6), .out(multiplexer_1_out), .sel(or_1_out));
  not not_1 (not_1_out, MMU_ST);
  nor nor_1 (nor_1_out, MMU_DATA, not_1_out);
  nor nor_2 (nor_2_out, MMU_DATA, MMU_ST);
  and and_1 (and_1_out, MMU_DATA, MMU_ST);
  and and_2 (and_2_out, MMU_DATA, not_1_out);
  RAM #(.addrWidth(13), .dataWidth(16), .trigger("high")) ram_1 (
    .addr({multiplexer_1_out, Ain[15:11]}), .we(nor_1_out), .oe(nor_2_out), .data({ram_1_data_2, ram_1_data}));
  RAM #(.addrWidth(13), .dataWidth(16), .trigger("high")) ram_2 (
    .addr({multiplexer_1_out, Ain[15:11]}), .we(and_1_out), .oe(and_2_out), .data({ram_1_data_2, ram_1_data}));
  assign A_PHYS[15:0] = not_2_out ? Ain : 16'bz;  // Controlled_Buffer controlled_buffer_1
  not not_2 (not_2_out, VMEM);
  assign {ram_1_data_2, ram_1_data} = MMU_ST ? Din : 16'bz;  // Controlled_Buffer controlled_buffer_2
  Pull_Resistor pull_resistor_1 (.node({ram_1_data_2, ram_1_data}));
  Multiplexer #(.width(23), .disabled("Z")) multiplexer_2 (
    .in0({ram_1_data[10:0], Ain[10:0], 1'b0}), .in1({ram_1_data, Ain[10:0]}), .out(A_PHYS[22:0]),
    .sel(MMU_DATA), .en(VMEM));
  not not_3 (not_3_out, ram_1_data_2[0]);
  and and_3 (PAGE_FAULT, not_3_out, VMEM, IO_LOAD);
  and and_4 (ILLEGAL_WRITE, ram_1_data_2[1], VMEM, IO_STORE);
  and and_5 (ILLEGAL_READ, ram_1_data_2[2], VMEM, IO_LOAD);
  and and_6 (out_16, ram_1_data_2[3], VMEM);

  assign A_PHYS[23] = MMU_DATA;
  // also tied to GND on the sheet: {A_PHYS[16], A_PHYS[17], A_PHYS[18], A_PHYS[19], A_PHYS[20], A_PHYS[21], A_PHYS[22]}

  // Other names for the same wires on the sheet: DATA = MMU_DATA

  // Notes on the sheet:
  //   Memory Management Unit (MMO)
  //   ~DATA & MMU_ST == ~(DATA | ~MMU_ST)
  //   ~DATA & ~MMU_ST == ~(DATA | MMU_ST)
  //   DATA & MMU_ST
  //   DATA & ~MMU_ST
  //   Looks like it needs some work (writing to page table etc)
  //   flags
endmodule

module reg_pc (
  input  RST,
  input  INC_PC,
  input  CLK,
  input  [15:0] PCin,
  input  EN_X_low,
  input  EN_Y_low,
  input  EN_Z_low,
  input  LOAD_low,
  output [15:0] Xout,
  output [15:0] Yout,
  output [15:0] Zout,
  output [15:0] PCout,
  output [15:0] out_13
);

  wire counter_1_carry, nor_1_out, not_1_out, not_2_out, not_3_out;
  wire [15:15] counter_1_q, pull_resistor_1_node;

  Pull_Resistor pull_resistor_1 (.node(pull_resistor_1_node[15]));
  nor nor_1 (nor_1_out, LOAD_low, EN_X_low);
  Counter #(.width(16), .max('hffff), .trigger("falling")) counter_1 (
    .clr(RST), .load(nor_1_out), .up(INC_PC), .count(INC_PC), .clk(CLK),
    .D({pull_resistor_1_node[15], PCin[15:1]}), .carry(counter_1_carry), .Q({counter_1_q[15], out_13[15:1]}));
  Pull_Resistor pull_resistor_2 (.node(out_13[0]));
  assign Xout = not_1_out ? out_13 : 16'bz;  // Controlled_Buffer controlled_buffer_1
  not not_1 (not_1_out, EN_X_low);
  assign Yout = not_2_out ? out_13 : 16'bz;  // Controlled_Buffer controlled_buffer_2
  not not_2 (not_2_out, EN_Y_low);
  assign Zout = not_3_out ? out_13 : 16'bz;  // Controlled_Buffer controlled_buffer_3
  not not_3 (not_3_out, EN_Z_low);

  assign PCout = out_13;

  // Notes on the sheet:
  //   Program Counter (PC)
endmodule

module reg_tristate (
  input  [15:0] Din,
  input  LD,
  input  CLK,
  input  RST,
  input  EN,
  output [15:0] Dout,
  output [15:0] out_7
);

  Register #(.width(16)) register_1 (.D(Din), .en(LD), .clk(CLK), .Q(out_7), .clr(RST));
  assign Dout = EN ? out_7 : 16'bz;  // Controlled_Buffer controlled_buffer_1

  // Notes on the sheet:
  //   Single User Register
endmodule

module reg_8bit_tristate (
  input  [7:0] in_1,
  input  LD,
  input  CLK,
  input  RST,
  input  EN,
  output [7:0] out_6,
  output [7:0] out_7
);

  Register register_1 (.D(in_1), .en(LD), .clk(CLK), .Q(out_7), .clr(RST));
  assign out_6 = EN ? out_7 : 8'bz;  // Controlled_Buffer controlled_buffer_1

  // Notes on the sheet:
  //   Tristate Register (8 bit)
endmodule

module counter_16_bit (
  input  [15:0] Din,
  input  LD_TIMER,
  input  CLK,
  input  RST,
  input  DECR,
  output CARRY,
  output [15:0] DATA
);

  wire and_1_out, not_1_out;

  not not_1 (not_1_out, CARRY);
  and and_1 (and_1_out, not_1_out, DECR);
  Counter #(.width(16), .max('hffff)) counter_1 (
    .clr(RST), .load(LD_TIMER), .up(1'b0), .count(and_1_out), .clk(CLK), .D(Din), .carry(CARRY), .Q(DATA));
  Pull_Resistor pull_resistor_1 (.node(CARRY));
endmodule

// IO
module io (
  input  [15:0] Din,
  input  [23:0] ADDR,
  input  STORE,
  input  LOAD,
  input  CLK,
  output [15:0] Dout
);

  wire and_1_out, and_2_out, IO_DEV;

  Comparator #(.width(15)) comparator_1 (.a(ADDR[23:9]), .b(15'h1ff), .eq(IO_DEV));  // open: gt, lt
  and and_1 (and_1_out, STORE, IO_DEV);
  and and_2 (and_2_out, IO_DEV, LOAD);

  // Notes on the sheet:
  //   Data RAM - Byte Addressable
endmodule

// RAM
module ram (
  input  [15:0] Din,
  input  [23:0] ADDR,
  input  BYPASS_RAM,
  input  CLK,
  input  STORE,
  input  LOAD,
  input  BYTE,
  output [15:0] Dout
);

  wire and_2_out, and_3_out, and_4_out, and_5_out, and_6_out, and_7_out, BYPASS_RAM_t, comparator_1_eq,
       comparator_2_eq, MAP_RAM, not_1_out, not_2_out, not_4_out, not_5_out, or_1_out;
  wire [7:0] rom_1_data, rom_2_data;
  wire [15:0] ram_1_data;

  not not_1 (not_1_out, BYPASS_RAM_t);
  not not_2 (not_2_out, LOAD);
  not not_3 (MAP_RAM, comparator_1_eq);
  Comparator #(.width(16)) comparator_1 (.a(ADDR[23:8]), .b(16'h1ff), .eq(comparator_1_eq));  // open: gt, lt
  Comparator #(.width(16)) comparator_2 (.a(ADDR[23:8]), .b({16{1'b0}}), .eq(comparator_2_eq));  // open: gt, lt
  and and_1 (BYPASS_RAM_t, comparator_2_eq, BYPASS_RAM);
  and and_2 (and_2_out, not_1_out, not_2_out, STORE, MAP_RAM);
  and and_3 (and_3_out, not_1_out, MAP_RAM, LOAD);
  and and_4 (and_4_out, and_2_out, ~CLK);  // AND_Gate
  RAM #(.addrWidth(23), .trigger("high")) ram_1 (
    .addr(ADDR[23:1]), .we(and_4_out), .oe(and_3_out), .data(ram_1_data[7:0]));
  RAM #(.addrWidth(23), .trigger("high")) ram_2 (
    .addr(ADDR[23:1]), .we(and_4_out), .oe(and_3_out), .data(ram_1_data[15:8]));
  ROM rom_1 (.addr(ADDR[8:1]), .data(rom_1_data));
  ROM rom_2 (.addr(ADDR[8:1]), .data(rom_2_data));
  not not_4 (not_4_out, ADDR[0]);
  not not_5 (not_5_out, BYTE);
  and and_5 (and_5_out, not_4_out, BYTE);
  and and_6 (and_6_out, ADDR[0], BYTE);
  Pull_Resistor pull_resistor_1 (.node(ram_1_data[7:0]));
  Pull_Resistor pull_resistor_2 (.node(ram_1_data[15:8]));
  or or_1 (or_1_out, and_5_out, not_5_out);
  Multiplexer #(.width(8), .disabled("Z"), .enable("false")) multiplexer_1 (
    .in1(rom_1_data), .out(ram_1_data[7:0]), .sel(and_7_out));  // open: in0
  Multiplexer #(.width(8), .disabled("Z"), .enable("false")) multiplexer_2 (
    .in1(rom_2_data), .out(ram_1_data[15:8]), .sel(and_7_out));  // open: in0
  assign Dout[7:0] = or_1_out ? ram_1_data[7:0] : 8'bz;  // Controlled_Buffer controlled_buffer_1
  assign Dout[7:0] = and_6_out ? ram_1_data[15:8] : 8'bz;  // Controlled_Buffer controlled_buffer_2
  assign Dout[15:8] = not_5_out ? ram_1_data[15:8] : 8'bz;  // Controlled_Buffer controlled_buffer_3
  and and_7 (and_7_out, BYPASS_RAM_t, MAP_RAM, LOAD);
  Multiplexer #(.width(16), .disabled("Z"), .enable("false")) multiplexer_3 (
    .in1(Din), .out(ram_1_data), .sel(and_4_out));  // open: in0

  // Notes on the sheet:
  //   Byte Addressable RAM
  //   This RAM circuit is no longer used
  //   contents of rom_1 (hex, n*v repeats v):
  //   f8
  //   contents of rom_2 (hex, n*v repeats v):
  //   f5 1 f0
  //   This RAM unit reads unaligned bytes and aligned 16 bit words.
  //   ~BYTE | (BYTE & ADDR_0)
  //   ~BYTE
  //   BYTE & ADDR_0
  //   these muxes are operating as tristate buffers due to a strange logisim bug
endmodule

// EXT
module sign_ext (
  input  [15:0] in_1,
  input  SIGN_EXT,
  input  EN_MMIO,
  output [15:0] out_4
);

  Multiplexer #(.width(16), .disabled("Z")) multiplexer_1 (
    .in0(in_1), .in1({{9{in_1[7]}}, in_1[6:0]}), .out(out_4), .sel(SIGN_EXT), .en(EN_MMIO));
endmodule

module test (
  input  [15:0] in_1,
  input  [23:0] in_2,
  input  [5:0] in_3
);

  wire [15:0] mmio_1_dout;

  mmio mmio_1 (
    .Dout(mmio_1_dout), .Store(in_3[4]), .Load(in_3[3]), .Byte(in_3[2]), .SignExt(in_3[1]), .Clk(in_3[0]));  // open: Din, Addr
  // Probe on mmio_1_dout
  main main_1 ();  // open: IRQ0, IRQ1, IRQ2, IRQ3
endmodule

module mmio (
  input  [15:0] Din,
  input  [23:0] Addr,
  input  Store,
  input  Load,
  input  Byte,
  input  SignExt,
  input  Clk,
  output [15:0] Dout
);

  wire and_4_out, and_5_out, and_6_out, and_7_out, and_8_out, and_9_out, FullWord, HighByte,
       HighByteAccessed, LowByte, LowByteAccessed, or_3_out, PhysRAM, PhysROM, pull_resistor_1_node,
       Ram0_OutEn, Ram0_WrEn, Ram1_OutEn, Ram1_WrEn, Rom0_OutEn, Rom1_OutEn;
  wire [7:0] HI_8, LO_8, rom_1_data, rom_2_data;

  and and_1 (LowByte, Addr[0], Byte);
  and and_2 (HighByte, ~Addr[0], Byte);  // AND_Gate
  not not_1 (FullWord, Byte);
  or or_1 (LowByteAccessed, LowByte, FullWord);
  or or_2 (HighByteAccessed, HighByte, FullWord);
  Pull_Resistor pull_resistor_1 (.node(pull_resistor_1_node));
  or or_3 (or_3_out, Addr[8], Addr[9], Addr[10], Addr[11], Addr[12], Addr[13], Addr[14], Addr[15], Addr[16], Addr[17], Addr[18], Addr[19], pull_resistor_1_node);
  and and_3 (PhysRAM, or_3_out, ~Addr[20]);  // AND_Gate
  nor nor_1 (PhysROM, PhysRAM, Addr[20]);
  and and_4 (and_4_out, Load, LowByteAccessed);
  and and_5 (and_5_out, Load, HighByte);
  and and_6 (and_6_out, Load, FullWord);
  assign LO_8 = and_8_out ? Din[7:0] : 8'bz;  // Controlled_Buffer controlled_buffer_1
  assign LO_8 = and_7_out ? Din[15:8] : 8'bz;  // Controlled_Buffer controlled_buffer_2
  assign HI_8 = and_9_out ? Din[15:8] : 8'bz;  // Controlled_Buffer controlled_buffer_3
  and and_7 (and_7_out, Store, HighByte);
  and and_8 (and_8_out, Store, LowByteAccessed);
  assign Dout[7:0] = and_4_out ? LO_8 : 8'bz;  // Controlled_Buffer controlled_buffer_4
  assign Dout[7:0] = and_5_out ? HI_8 : 8'bz;  // Controlled_Buffer controlled_buffer_5
  assign Dout[15:8] = and_6_out ? HI_8 : 8'bz;  // Controlled_Buffer controlled_buffer_6
  // Probe on HI_8
  // Probe on LO_8
  and and_9 (and_9_out, Store, FullWord);
  assign Dout[15:8] = SignExt ? {8{Dout[7]}} : 8'bz;  // Controlled_Buffer controlled_buffer_7
  RAM #(.addrWidth(20), .trigger("high")) ram_1 (.addr(Addr[20:1]), .we(Ram1_WrEn), .oe(Ram1_OutEn), .data(HI_8));
  ROM #(.addrWidth(7)) rom_1 (.addr(Addr[7:1]), .data(rom_1_data));
  and and_10 (Rom0_OutEn, LowByteAccessed, PhysROM, Load);
  and and_11 (Rom1_OutEn, HighByteAccessed, PhysROM, Load);
  assign HI_8 = Rom1_OutEn ? rom_1_data : 8'bz;  // Controlled_Buffer controlled_buffer_8
  and and_12 (Ram0_OutEn, LowByteAccessed, PhysRAM, Load);
  and and_13 (Ram1_OutEn, HighByteAccessed, PhysRAM, Load);
  RAM #(.addrWidth(20), .trigger("high")) ram_2 (.addr(Addr[20:1]), .we(Ram0_WrEn), .oe(Ram0_OutEn), .data(LO_8));
  ROM #(.addrWidth(7)) rom_2 (.addr(Addr[7:1]), .data(rom_2_data));
  and and_14 (Ram0_WrEn, LowByteAccessed, PhysRAM, Store, ~Clk);  // AND_Gate
  and and_15 (Ram1_WrEn, HighByteAccessed, PhysRAM, Store, ~Clk);  // AND_Gate
  assign LO_8 = Rom0_OutEn ? rom_2_data : 8'bz;  // Controlled_Buffer controlled_buffer_9

  // Other names for the same wires on the sheet: Even = Addr[0]; PhysIO = Addr[20]

  // Notes on the sheet:
  //   MMIO (RAM / ROM, IO)
  //   Inputs
  //   Logical Wires
  //   Address Range Test
  //   Bus Interface, Bidirectional
  //   contents of rom_1 (hex, n*v repeats v):
  //   f5 1 77 f0
  //   RAM / ROM Circuit Control
  //   contents of rom_2 (hex, n*v repeats v):
  //   f8 0 66
endmodule

module transceiver (
  input  Dir,
  input  OE,
  input  [7:0] LeftIn,
  input  [7:0] RightIn,
  output [7:0] RightOut,
  output [7:0] LeftOut
);

  wire and_1_out, and_2_out;

  and and_1 (and_1_out, Dir, OE);
  assign RightOut = and_1_out ? LeftIn : 8'bz;  // Controlled_Buffer controlled_buffer_1
  assign LeftOut = and_2_out ? RightIn : 8'bz;  // Controlled_Buffer controlled_buffer_2
  and and_2 (and_2_out, ~Dir, OE);  // AND_Gate
endmodule
